# Fritzing sketch UVG_ultrasound_schematic (saved by Fritzing 0.9.3b)
breadboards: 1

parts:
  Part1 = Arduino Uno (Rev3)
  HC-SR04_FRONT = HC-SR04 Ultrasonic Distance Sensor
  HC-SR04_REAR = HC-SR04 Ultrasonic Distance Sensor
  HC-SR04_LEFT = HC-SR04 Ultrasonic Distance Sensor
  HC-SR04_RIGHT = HC-SR04 Ultrasonic Distance Sensor
  HC-SR04_TOP = HC-SR04 Ultrasonic Distance Sensor

nets:
  N1: Part1.D8, HC-SR04_RIGHT.TRIG
  N2: Part1.D9_PWM, HC-SR04_RIGHT.GND
  N3: Part1.D10_PWM/SS, HC-SR04_TOP.TRIG
  N4: Part1.D11_PWM/MOSI, HC-SR04_TOP.GND
  N5: Part1.GND, HC-SR04_FRONT.ECHO, HC-SR04_REAR.ECHO, HC-SR04_LEFT.ECHO, HC-SR04_RIGHT.ECHO, HC-SR04_TOP.ECHO
  N6: Part1.D2, HC-SR04_FRONT.TRIG
  N7: Part1.D3_PWM, HC-SR04_FRONT.GND
  N8: Part1.D4, HC-SR04_REAR.TRIG
  N9: Part1.D5_PWM, HC-SR04_REAR.GND
  N10: Part1.D6_PWM, HC-SR04_LEFT.TRIG
  N11: Part1.D7, HC-SR04_LEFT.GND
  VCC: Part1.5V, HC-SR04_FRONT.VCC, HC-SR04_REAR.VCC, HC-SR04_LEFT.VCC, HC-SR04_RIGHT.VCC, HC-SR04_TOP.VCC
